# Fritzing sketch nodemcu-wifibot (saved by Fritzing 0.9.4)
breadboards: 1

parts:
  part = ESP8266 NodeMCU LoLin module
  SN754410_or_L293 = H-Bridge [package=THT]
  6V_battery_(4_x_AAA) = 4 x AAA Battery Mount
  power_switch = Toggle Switch [package=THT]
  RIGHT_motor = DC Motor
  LEFT_motor = DC Motor

nets:
  N1: part.D1, SN754410_or_L293.1A
  N2: part.D2, SN754410_or_L293.2A
  N3: part.D4, SN754410_or_L293.1_2EN
  GND: part.GND, SN754410_or_L293.GND1, SN754410_or_L293.GND2, SN754410_or_L293.GND3, SN754410_or_L293.GND4, 6V_battery_(4_x_AAA).-
  N4: part.D5, SN754410_or_L293.4A
  N5: part.D6, SN754410_or_L293.3A
  N6: part.D7, SN754410_or_L293.3_4EN
  N7: part.Vin, SN754410_or_L293.VCC2, SN754410_or_L293.VCC1, power_switch.L1
  N8: SN754410_or_L293.1Y, LEFT_motor.pin_2
  N9: SN754410_or_L293.2Y, LEFT_motor.pin_1
  N10: SN754410_or_L293.3Y, RIGHT_motor.pin_2
  N11: SN754410_or_L293.4Y, RIGHT_motor.pin_1
  N12: 6V_battery_(4_x_AAA).+, power_switch.COM

custom parts:
  ESP8266 NodeMCU LoLin module: ESP8266 based NodeMCU
